# Fritzing sketch esp32_basic_blink (saved by Fritzing 0.9.4)
breadboards: 1

parts:
  LED1 = LED - 5mm [color="Red (633nm)" package="5 mm [THT]"]
  R1 = Resistor [tolerance=±5% resistance=330 package=THT]
  U1 = ESP32-devkit-V4 [part_number=ESP32-WROOM-32U]

nets:
  N1: LED1.cathode, U1.GND
  N2: LED1.anode, R1.Pin_0
  N3: R1.Pin_1, U1.GPIO23

custom parts:
  ESP32-devkit-V4: ESP-WROOM-32 Development Board 2.4GHz Dual-Mode WiFi + Bluetooth Dual Cores Microcontroller
