# Fritzing sketch esp32_basic_dht (saved by Fritzing 0.9.4)
breadboards: 1

parts:
  LED1 = LED - 5mm [color="Green (555nm)" part_number="WiFi conn" package="5 mm [THT]"]
  R1 = Resistor [tolerance=±5% resistance=330 package=THT]
  U1 = ESP32-devkit-V4 [part_number=ESP32-WROOM-32U]
  DHT22_1 = DHT22 Humidity and Temperature Sensor
  R2 = Resistor [tolerance=±5% resistance=10k package=THT]
  DHT22_2 = DHT22 Humidity and Temperature Sensor
  R3 = Resistor [tolerance=±5% resistance=10k package=THT]
  LED2 = LED - 5mm [color="Yellow (595nm)" part_number="MQTT conn" package="5 mm [THT]"]
  R4 = Resistor [tolerance=±5% resistance=330 package=THT]

nets:
  GND: LED1.cathode, U1.GND, DHT22_1.GND, DHT22_2.GND, LED2.cathode
  N1: LED1.anode, R1.Pin_0
  N2: R1.Pin_1, U1.GPIO23
  VDD: U1.VIN, DHT22_1.VDD, R2.Pin_1, DHT22_2.VDD, R3.Pin_1
  N3: U1.GPIO15, DHT22_1.DATA, R2.Pin_0
  N4: U1.GPIO2, DHT22_2.DATA, R3.Pin_0
  N5: U1.GPIO22, R4.Pin_1
  N6: LED2.anode, R4.Pin_0

custom parts:
  ESP32-devkit-V4: ESP-WROOM-32 Development Board 2.4GHz Dual-Mode WiFi + Bluetooth Dual Cores Microcontroller
