# Fritzing sketch esp32_interrupts (saved by Fritzing 0.9.4)
breadboards: 1

parts:
  LED1 = LED - 5mm [color="Red (633nm)" package="5 mm [THT]"]
  R1 = Resistor [tolerance=±5% resistance=330 package=THT]
  U1 = ESP32-devkit-V4 [part_number=ESP32-WROOM-32U]
  S1 = Pushbutton [package="[THT]"]
  S2 = Pushbutton [package="[THT]"]
  R2 = Resistor [tolerance=±5% resistance=10k package=THT]
  C1 = Ceramic Capacitor [capacitance=10nF package="100 mil [THT, multilayer]"]
  S3 = Pushbutton [package="[THT]"]
  S4 = Pushbutton [package="[THT]"]
  R3 = Resistor [tolerance=±5% resistance=220 package=THT]
  R4 = Resistor [tolerance=±5% resistance=220 package=THT]

nets:
  N1: LED1.cathode, U1.GND, S1.Pin_3, S1.Pin_4, R2.Pin_0, S4.Pin_3, S4.Pin_4, R4.Pin_1
  N2: LED1.anode, R1.Pin_0
  N3: R1.Pin_1, U1.GPIO23
  N4: U1.GPIO32, S1.Pin_1, S1.Pin_2
  N5: U1.GPIO33, S2.Pin_3, S2.Pin_4, R2.Pin_1, C1.0
  N6: U1.VIN, S2.Pin_1, S2.Pin_2, C1.1, S3.Pin_1, S3.Pin_2, R3.Pin_0
  N7: S3.Pin_3, S3.Pin_4, R4.Pin_0
  N8: S4.Pin_1, S4.Pin_2, R3.Pin_1

notes:
  active low - signal goes from high (use internal Pullup) to low when button is pressed
  active high - signal goes from low to high when button is pressed.
  Capacitor for debouncing.
  Pull-Up vs. Pull-Down
  restistor

custom parts:
  ESP32-devkit-V4: ESP-WROOM-32 Development Board 2.4GHz Dual-Mode WiFi + Bluetooth Dual Cores Microcontroller
